# Fritzing sketch MicroViewClock_DS3231_schema (saved by Fritzing 0.9.0b)
breadboards: 1

parts:
  V1 = DC Power [voltage=5V]
  MV1 = MicroView [part_number=MicroView package="16pin wide"]
  BB-3231RTC1 = DS3231 RTC Module

nets:
  5V: V1.V+, MV1.5V, BB-3231RTC1.VCC
  GND: V1.V-, MV1.GND, BB-3231RTC1.GND
  N1: MV1.D3, BB-3231RTC1.SCL
  N2: MV1.D5, BB-3231RTC1.SDA

custom parts:
  MicroView: MicroView - Chip-sized Arduino with OLED display.
  DS3231 RTC Module: The DS3231 Real Time Clock IC has an internal crystal and a switched bank of tuning capacitors. The temperature of the crystal is continously monitored, and the capacitors are adjusted to maintain a stable frequency. Other RTC solutions may drift minutes per month, especially in extreme temperature ranges. However, this 3231 RTC module will drift less than a minute per year. This makes DS3231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
